// Logisim project single_cycle_shifter.circ as structural Verilog: 1 circuit, main circuit single_cycle_shifter
module single_cycle_shifter (
  input  in_1,
  input  [2:0] in_2,
  input  [31:0] in_3,
  input  [4:0] in_4,
  output [31:0] out_5
);

  wire and_1_out, and_2_out, and_5_out, and_6_out, and_8_out, and_9_out, and_11_out, and_12_out, and_14_out,
       and_15_out, not_1_out, not_2_out, not_3_out, not_4_out, not_5_out, shift_to_left, shift_to_right;
  wire [31:0] controlled_buffer_1_out, controlled_buffer_4_out, controlled_buffer_7_out,
       controlled_buffer_10_out;
  wire [31:31] and_3_out, and_4_out, and_7_out, and_10_out, and_13_out;

  Decoder #(.enable("false"), .select(3)) decoder_1 (
    .out1(shift_to_left), .out5(shift_to_right), .sel(in_2));  // open: out0, out2, out3, out4, out6, out7
  not not_1 (not_1_out, in_4[0]);
  assign controlled_buffer_1_out = and_1_out ? {in_3[30:0], 1'b0} : 32'bz;  // Controlled_Buffer controlled_buffer_1
  and and_1 (and_1_out, shift_to_left, in_4[0]);
  assign controlled_buffer_1_out = not_1_out ? in_3 : 32'bz;  // Controlled_Buffer controlled_buffer_2
  and and_2 (and_2_out, shift_to_right, in_4[0]);
  assign controlled_buffer_1_out = and_2_out ? {and_3_out[31], in_3[31:1]} : 32'bz;  // Controlled_Buffer controlled_buffer_3
  and and_3 (and_3_out[31], in_3[31], in_1);
  assign controlled_buffer_4_out = not_2_out ? controlled_buffer_1_out : 32'bz;  // Controlled_Buffer controlled_buffer_4
  not not_2 (not_2_out, in_4[1]);
  and and_4 (and_4_out[31], controlled_buffer_1_out[31], in_1);
  assign controlled_buffer_4_out = and_5_out ? {controlled_buffer_1_out[29:0], 2'b00} : 32'bz;  // Controlled_Buffer controlled_buffer_5
  and and_5 (and_5_out, shift_to_left, in_4[1]);
  and and_6 (and_6_out, shift_to_right, in_4[1]);
  assign controlled_buffer_4_out = and_6_out ? {{2{and_4_out[31]}}, controlled_buffer_1_out[31:2]} : 32'bz;  // Controlled_Buffer controlled_buffer_6
  assign controlled_buffer_7_out = not_3_out ? controlled_buffer_4_out : 32'bz;  // Controlled_Buffer controlled_buffer_7
  not not_3 (not_3_out, in_4[2]);
  and and_7 (and_7_out[31], controlled_buffer_4_out[31], in_1);
  assign controlled_buffer_7_out = and_8_out ? {controlled_buffer_4_out[27:0], 4'b0000} : 32'bz;  // Controlled_Buffer controlled_buffer_8
  and and_8 (and_8_out, shift_to_left, in_4[2]);
  and and_9 (and_9_out, shift_to_right, in_4[2]);
  assign controlled_buffer_7_out = and_9_out ? {{4{and_7_out[31]}}, controlled_buffer_4_out[31:4]} : 32'bz;  // Controlled_Buffer controlled_buffer_9
  assign controlled_buffer_10_out = not_4_out ? controlled_buffer_7_out : 32'bz;  // Controlled_Buffer controlled_buffer_10
  not not_4 (not_4_out, in_4[3]);
  and and_10 (and_10_out[31], controlled_buffer_7_out[31], in_1);
  assign controlled_buffer_10_out = and_11_out ? {controlled_buffer_7_out[23:0], {8{1'b0}}} : 32'bz;  // Controlled_Buffer controlled_buffer_11
  and and_11 (and_11_out, shift_to_left, in_4[3]);
  and and_12 (and_12_out, shift_to_right, in_4[3]);
  assign controlled_buffer_10_out = and_12_out ? {{8{and_10_out[31]}}, controlled_buffer_7_out[31:8]} : 32'bz;  // Controlled_Buffer controlled_buffer_12
  assign out_5 = not_5_out ? controlled_buffer_10_out : 32'bz;  // Controlled_Buffer controlled_buffer_13
  not not_5 (not_5_out, in_4[4]);
  and and_13 (and_13_out[31], controlled_buffer_10_out[31], in_1);
  assign out_5 = and_14_out ? {controlled_buffer_10_out[15:0], {16{1'b0}}} : 32'bz;  // Controlled_Buffer controlled_buffer_14
  and and_14 (and_14_out, shift_to_left, in_4[4]);
  and and_15 (and_15_out, shift_to_right, in_4[4]);
  assign out_5 = and_15_out ? {{16{and_13_out[31]}}, controlled_buffer_10_out[31:16]} : 32'bz;  // Controlled_Buffer controlled_buffer_15
  // Probe on out_5

  // Other names for the same wires on the sheet: input_data[31:0] = in_3; funct3[2:0] = in_2; is_arithmetic = in_1;
  //   shift_by[4:0] = in_4; shifted_data[31:0] = out_5

  // Notes on the sheet:
  //   Inputs
  //   input data (from RB0)
  //   shift by (from RB1)
  //   | ins | func3 | i |
  //   | SLL | 001 | x |
  //   | SRL | 101 | 0 |
  //   | SRA | 101 | 1 |
  //   i: 31st bit of ins
  //   funct3
  //   Outputs
endmodule
